# Fritzing sketch prototypeCircuit (saved by Fritzing 0.9.4)
circuit board: 8.46667cm x 5.64444cm
breadboards: 1

parts:
  Resistor = Resistor [tolerance=±5% resistance=150 package="2512 [SMD]"]
  Vibe_Module = Vibration Motor- ROB-08449 [package=vibe-motor-10mm]
  NPN_Transistor = NPN-Transistor [package="TO92 [THT]"]
  Capacitor = Ceramic Capacitor [capacitance=100nF package="200 mil [THT, multilayer]"]
  Diode = Diode [package=diode-hv]
  Resistor_2 = Resistor [tolerance=±5% resistance=1k package="2010 [SMD]"]
  Stretch_Sensor = Textile Stretch Sensor
  LED = LED - 5mm [color="Red (633nm)" package="5 mm [THT]"]
  Resistor_3 = Resistor [tolerance=±5% resistance=220 package=THT]
  Microcontroller = Lilypad Arduino Board

nets:
  N1: Resistor.Pin_0, NPN_Transistor.E, LED.anode, Microcontroller.GND
  N2: Resistor.Pin_1, Stretch_Sensor.pin_1, Microcontroller.A2
  N3: Vibe_Module.+, Capacitor.0, Diode.C, Stretch_Sensor.pin_0, Microcontroller.VCC
  N4: Vibe_Module.-, NPN_Transistor.C, Capacitor.1, Diode.A
  N5: NPN_Transistor.B, Resistor_2.Pin_1
  N6: Resistor_2.Pin_0, Microcontroller.D3
  N7: LED.cathode, Resistor_3.Pin_1
  N8: Resistor_3.Pin_0, Microcontroller.D2
